# Fritzing sketch veryvell-shield (saved by Fritzing 0.9.3b)
stripboards: 1

parts:
  U1 = ESP8266 WiFi Module [part_number=ESP8266]
  arduino = Arduino Uno (Rev3)
  C1_5V = Electrolytic Capacitor [capacitance=1µF voltage=35V package="100 mil [THT, electrolytic]"]
  R2 = Resistor [tolerance=±5% resistance=2k package="2010 [SMD]"]
  R1 = Resistor [tolerance=±5% resistance=1k package=THT]
  U4 = Mystery Part - 3 pins [chip_label="1117 3V3" package=THT]
  U5 = mystery part, 4 pins [chip_label=?]
  J1 = female pin header, 3 pins [form="♀ (female)"]  # not connected
  C2_3_3V = Electrolytic Capacitor [capacitance=1µF voltage=35V package="100 mil [THT, electrolytic]"]

nets:
  N1: U1.RXD, R2.Pin_0, R1.Pin_1
  VCC: U1.VCC, U4.3V3, C2_3_3V.+
  N2: U1.RST, U1.CH_PD
  GND: U1.GND, arduino.GND, C1_5V.-, R2.Pin_1, U4.GND, U5.pin1, C2_3_3V.-
  N3: U1.TXD, arduino.D2
  N4: arduino.A4/SDA, arduino.D1/TX
  N5: arduino.A5/SCL, arduino.D0/RX
  N6: arduino.D3_PWM, R1.Pin_0
  N7: arduino.D5_PWM, U5.pin2
  N8: arduino.D6_PWM, U5.pin3
  5V: arduino.5V, C1_5V.+, U4.VCC, U5.pin4

custom parts:
  ESP8266 WiFi Module: Generic WiFi Module based on the ESP8266 with onboard PCB antenna and UART communications
  Mystery Part - 3 pins: A dummy, proxy, ersatz, stand-in part for whatever you want. With 3 pins on a 100 mil inline pin header footprint.
